# Fritzing sketch Schema fritzing (saved by Fritzing 0.9.3b)

parts:
  Composant1 = Arduino Uno (Rev3)
  GY1 = GY-521 (MPU-6050) [form="♀ (female)" package=THT]
  VCC1 = Battery
  M1 = DC Motor  # not connected
  M2 = DC Motor  # not connected
  L298N1 = L298N DC motor driver
  VCC2 = Battery  # not connected

nets:
  N1: Composant1.D8, L298N1.IN3
  N2: Composant1.D9_PWM, L298N1.IN4
  N3: Composant1.D10_PWM/SS, L298N1.ENB
  N4: Composant1.A4/SDA, GY1.pin4
  N5: Composant1.A5/SCL, GY1.pin3
  N6: Composant1.D2, GY1.pin8
  N7: Composant1.D5_PWM, L298N1.ENA
  N8: Composant1.D6_PWM, L298N1.IN1
  N9: Composant1.D7, L298N1.IN2
  N10: Composant1.3V3, GY1.pin1
  N11: Composant1.5V, VCC1.+
  N12: GY1.pin2, VCC1.-

custom parts:
  GY-521 (MPU-6050): Placa GY-521 basada en conjunto de acelerómetro+giroscopios MPU-6050
  L298N DC motor driver: 2x DC motor driver with 78M05 positive voltage regulator (7..35 V) L298N: max 46 V, 2 A Set 5 V Enable jumper to enable 5 V regultor (needed for the L298N) and +5 V output at screw terminal or supply external +5 V at screw terminal Set ENA and/or ENB to +5 V to enable motor permanently or supply ENA and/or ENB with PWM signal IN1 and IN2 set rotation directory for motor A (OUT1/OUT2) IN2 and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
